# Fritzing sketch termometro (saved by Fritzing 0.7.12b)
breadboards: 1

parts:
  Arduino1 = Arduino
  T1 = TMP36 Temperature Sensor [package="TO92 [THT]"]
  R1 = Trimmer Potentiometer [maximum_resistance=10kΩ package=THT]
  LCD1 = LCD screen
  R2 = Resistor [tolerance=±5% resistance=220 package=THT]

nets:
  N1: Arduino1.D12, LCD1.RS
  N2: Arduino1.D11, LCD1.E
  N3: Arduino1.D5, LCD1.DB4
  N4: Arduino1.D4, LCD1.DB5
  N5: Arduino1.D3, LCD1.DB6
  N6: Arduino1.D2, LCD1.DB7
  +5V: Arduino1.+5V, T1.+Vs, R1.leg1, LCD1.VDD, R2.Pin_1
  GND: Arduino1.GND, T1.GND, R1.leg2, LCD1.VSS, LCD1.R/W, LCD1.LED-
  N7: Arduino1.A0, T1.Vout
  N8: R1.wiper, LCD1.V0
  N9: LCD1.LED+, R2.Pin_0
